// Digital circuit circuito_semaforo.dig as structural Verilog
module circuito_semaforo (
  input  clk
);

  wire and_1_out, and_2_out, and_3_out, and_4_out, and_5_out, and_6_out, and_7_out, and_8_out, and_9_out,
       and_10_out, and_11_out, and_12_out, and_13_out, and_14_out, and_15_out, and_16_out, and_17_out,
       and_18_out, and_19_out, and_20_out, and_21_out, and_22_out, and_23_out, and_24_out, button_1_out,
       nand_1_out, nand_2_out, nand_3_out, nand_4_out, or_1_out, or_2_out, or_3_out, or_4_out, or_5_out,
       or_6_out, Zn0_q, Zn1_q, Zn2_q;

  Button button_1 (.out(button_1_out));
  nand nand_1 (nand_1_out, button_1_out, 1'b1);
  nand nand_2 (nand_2_out, 1'b1, or_6_out);
  nand nand_3 (nand_3_out, nand_1_out, nand_4_out);
  nand nand_4 (nand_4_out, nand_3_out, nand_2_out);
  and and_1 (and_1_out, ~Zn1_q, ~Zn2_q, ~nand_3_out);  // And
  and and_2 (and_2_out, nand_3_out, ~Zn0_q, ~Zn1_q, Zn2_q);  // And
  and and_3 (and_3_out, ~Zn2_q, nand_3_out, Zn1_q);  // And
  and and_4 (and_4_out, Zn0_q, Zn1_q, Zn2_q);
  and and_5 (and_5_out, ~Zn0_q, Zn1_q, ~Zn2_q);  // And
  and and_6 (and_6_out, ~Zn2_q, nand_3_out);  // And
  and and_7 (and_7_out, ~Zn2_q, Zn0_q, ~Zn1_q);  // And
  and and_8 (and_8_out, ~Zn0_q, Zn1_q);  // And
  and and_9 (and_9_out, ~Zn0_q, nand_3_out, ~Zn1_q);  // And
  and and_10 (and_10_out, Zn0_q, Zn1_q);
  and and_11 (and_11_out, ~Zn0_q, ~Zn1_q, ~Zn2_q);  // And
  and and_12 (and_12_out, ~Zn1_q, Zn0_q, ~Zn2_q);  // And
  and and_13 (and_13_out, ~Zn0_q, Zn1_q, Zn2_q);  // And
  and and_14 (and_14_out, Zn0_q, ~Zn2_q, Zn1_q);  // And
  and and_15 (and_15_out, ~Zn0_q, ~Zn1_q, Zn2_q);  // And
  and and_16 (and_16_out, Zn1_q, Zn2_q, Zn0_q);
  and and_17 (and_17_out, ~Zn0_q, ~Zn2_q, Zn1_q);  // And
  and and_18 (and_18_out, ~Zn1_q, Zn0_q, Zn2_q);  // And
  or or_1 (or_1_out, and_1_out, and_2_out, and_3_out, and_4_out, and_5_out);
  or or_2 (or_2_out, and_6_out, and_7_out, and_8_out);
  or or_3 (or_3_out, and_9_out, and_10_out);
  or or_4 (or_4_out, and_12_out, and_13_out);
  or or_5 (or_5_out, and_15_out, and_16_out);
  or or_6 (or_6_out, and_17_out, and_18_out);
  D_FF Zn0 (.D(or_1_out), .C(clk), .Q(Zn0_q));  // open: nQ
  D_FF Zn1 (.D(or_2_out), .C(clk), .Q(Zn1_q));  // open: nQ
  D_FF Zn2 (.D(or_3_out), .C(clk), .Q(Zn2_q));  // open: nQ
  and and_19 (and_19_out, ~and_11_out, or_4_out);  // And
  and and_20 (and_20_out, ~or_4_out, and_11_out);  // And
  and and_21 (and_21_out, ~and_11_out, ~or_4_out);  // And
  // RGBLED rgbled_1: pin names not known; wires that end beside it: and_21_out, 1'b0, 1'b0, and_19_out
  // RGBLED rgbled_2: pin names not known; wires that end beside it: and_19_out, 1'b0, 1'b0
  // RGBLED rgbled_3: pin names not known; wires that end beside it: and_20_out, 1'b0
  and and_22 (and_22_out, ~or_5_out, and_14_out);  // And
  and and_23 (and_23_out, ~and_14_out, or_5_out);  // And
  and and_24 (and_24_out, ~and_14_out, ~or_5_out);  // And
  // RGBLED rgbled_4: pin names not known; wires that end beside it: and_24_out, 1'b0, 1'b0, and_23_out
  // RGBLED rgbled_5: pin names not known; wires that end beside it: and_23_out, 1'b0, 1'b0
  // RGBLED rgbled_6: pin names not known; wires that end beside it: and_22_out, 1'b0
  // RGBLED rgbled_7: pin names not known; wires that end beside it: and_21_out, 1'b0, 1'b0, and_19_out
  // RGBLED rgbled_8: pin names not known; wires that end beside it: and_19_out, 1'b0, 1'b0
  // RGBLED rgbled_9: pin names not known; wires that end beside it: and_20_out, 1'b0
  // Not not_1 has open pins: in=or_6_out, out=open
  // Not not_2 has open pins: in=or_6_out, out=open
  // RGBLED rgbled_10: pin names not known; wires that end beside it: 1'b0, 1'b0, 1'b0
  // RGBLED rgbled_11: pin names not known; wires that end beside it: or_6_out, 1'b0
  // RGBLED rgbled_12: pin names not known; wires that end beside it: 1'b0, 1'b0, 1'b0
  // RGBLED rgbled_13: pin names not known; wires that end beside it: or_6_out, 1'b0

  // Notes on the sheet:
  //   A1
  //   B1
  //   A0
  //   B0
  //   C
  //   Z0n+1
  //   Z1n+1
  //   Z2n+1
  //   Semaforo 1
  //   Semaforo 2
  //   Semaforo 3
  //   Pedestre
endmodule
